// Logisim project 1-bit-ALU-n.circ as structural Verilog: 2 circuits, main circuit 1 bit ALU
module _1_bit_ALU (
  input  A,
  input  B,
  input  Cin,
  input  [1:0] Op,
  output Function_Output,
  output Cout
);

  wire adder_1_out, and_1_out, not_1_out, or_1_out;

  and and_1 (and_1_out, A, B);
  or or_1 (or_1_out, A, B);
  not not_1 (not_1_out, B);
  Adder #(.width(1)) adder_1 (.a(A), .b(B), .out(adder_1_out), .cin(Cin), .cout(Cout));
  Multiplexer #(.select(2), .enable("false")) multiplexer_1 (
    .in0(and_1_out), .in1(or_1_out), .in2(not_1_out), .in3(adder_1_out), .out(Function_Output), .sel(Op));
endmodule

module _4_Bit_ALU (
  input  [1:0] in_1,
  input  [3:0] A,
  input  [3:0] B,
  output [3:0] out_4
);

  _1_bit_ALU u_1_bit_alu_1 (.Function_Output(out_4[0]), .A(A[0]), .B(B[0]));  // open: Cin, Op, Cout
  _1_bit_ALU u_1_bit_alu_2 (.Function_Output(out_4[1]), .A(A[1]), .B(B[1]));  // open: Cin, Op, Cout
  _1_bit_ALU u_1_bit_alu_3 (.A(A[2]), .B(B[2]), .Op(in_1));  // open: Function_Output, Cin, Cout
  _1_bit_ALU u_1_bit_alu_4 (.Function_Output(out_4[3]), .A(A[3]), .B(B[3]), .Op(in_1));  // open: Cin, Cout
endmodule
